// Digital circuit 2_bit_unsigned_multiplier.dig as structural Verilog
module _2_bit_unsigned_multiplier (
  input  A0,
  input  B0,
  input  A1,
  input  B1,
  output P0,
  output P1,
  output P2,
  output P3,
  output AxB
);

  wire and_3_out, and_4_out, and_5_out;

  and and_1 (AxB, A0, B0);
  and and_2 (P3, A1, B1);
  and and_3 (and_3_out, A0, B1);
  and and_4 (and_4_out, B0, A1);
  xor xor_1 (P1, and_3_out, and_4_out);
  and and_5 (and_5_out, and_3_out, and_4_out);
  xor xor_2 (P2, and_5_out, P3);

  assign P0 = AxB;
endmodule
