// Digital circuit 4_bit_adder_subtractor.dig as structural Verilog
module _4_bit_adder_subtractor (
  input  [3:0] A,
  input  [3:0] B,
  input  Toggle,
  input  C_in,
  output [3:0] sum,
  output C_out
);

  wire _1_bit_adder_2_carry_out, _1_bit_adder_3_carry_out, _1_bit_adder_4_carry_out, xor_1_out, xor_2_out,
       xor_3_out, xor_4_out;

  xor xor_1 (xor_1_out, Toggle, B[3]);
  _1_bit_adder _1_bit_adder_1 (
    .A(A[3]), .B(xor_1_out), .carry_in(_1_bit_adder_2_carry_out), .sum(sum[3]), .carry_out(C_out));
  xor xor_2 (xor_2_out, Toggle, B[2]);
  _1_bit_adder _1_bit_adder_2 (
    .A(A[2]), .B(xor_2_out), .carry_in(_1_bit_adder_3_carry_out), .sum(sum[2]),
    .carry_out(_1_bit_adder_2_carry_out));
  xor xor_3 (xor_3_out, Toggle, B[1]);
  _1_bit_adder _1_bit_adder_3 (
    .A(A[1]), .B(xor_3_out), .carry_in(_1_bit_adder_4_carry_out), .sum(sum[1]),
    .carry_out(_1_bit_adder_3_carry_out));
  xor xor_4 (xor_4_out, Toggle, B[0]);
  _1_bit_adder _1_bit_adder_4 (
    .A(A[0]), .B(xor_4_out), .carry_in(C_in), .sum(sum[0]), .carry_out(_1_bit_adder_4_carry_out));
endmodule
