// Digital circuit 4_bit_ripple_carry_adder.dig as structural Verilog
module _4_bit_ripple_carry_adder (
  input  Carry_in,
  input  [3:0] B,
  input  [3:0] A,
  output [3:0] sum,
  output Carry_out
);

  wire _1_bit_adder_2_carry_out, _1_bit_adder_3_carry_out, _1_bit_adder_4_carry_out;

  _1_bit_adder _1_bit_adder_1 (
    .A(A[3]), .B(B[3]), .carry_in(_1_bit_adder_2_carry_out), .sum(sum[3]), .carry_out(Carry_out));
  _1_bit_adder _1_bit_adder_2 (
    .A(A[2]), .B(B[2]), .carry_in(_1_bit_adder_3_carry_out), .sum(sum[2]),
    .carry_out(_1_bit_adder_2_carry_out));
  _1_bit_adder _1_bit_adder_3 (
    .A(A[1]), .B(B[1]), .carry_in(_1_bit_adder_4_carry_out), .sum(sum[1]),
    .carry_out(_1_bit_adder_3_carry_out));
  _1_bit_adder _1_bit_adder_4 (
    .A(A[0]), .B(B[0]), .carry_in(Carry_in), .sum(sum[0]), .carry_out(_1_bit_adder_4_carry_out));
endmodule
