// Digital circuit general_purpose_register.dig as structural Verilog
module general_purpose_register (
  input  [3:0] Input,
  input  [1:0] Store_Clear_Load_Increment,
  input  clock,
  output [3:0] Output
);

  wire [3:0] multiplexer_1_out;

  Multiplexer #(.Selector_Bits(2), .Bits(4)) multiplexer_1 (
    .sel(Store_Clear_Load_Increment), .in_0(4'b0000), .in_1(Input), .in_2(Output), .in_3(4'b1111),
    .out(multiplexer_1_out));
  D_FF d_ff_1 (.D(multiplexer_1_out[3]), .C(clock), .Q(Output[3]));  // open: nQ
  D_FF d_ff_2 (.D(multiplexer_1_out[2]), .C(clock), .Q(Output[2]));  // open: nQ
  D_FF d_ff_3 (.D(multiplexer_1_out[1]), .C(clock), .Q(Output[1]));  // open: nQ
  D_FF d_ff_4 (.D(multiplexer_1_out[0]), .C(clock), .Q(Output[0]));  // open: nQ

  // Notes on the sheet:
  //   Store_Clear_Load_Increment: 0 -> clear
  //   1 -> store input
  //   2 -> load
  //   3 -> set to F
endmodule
