// Digital circuit program_counter.dig as structural Verilog
module program_counter (
  input  [3:0] Input,
  input  [1:0] Store_Clear_Load_Increment,
  input  clock,
  input  [3:0] Input_B,
  output [3:0] Output
);

  wire [3:0] add_1_s, multiplexer_1_out;

  Add #(.Bits(4)) add_1 (.a(Output), .b(Input_B), .c_i(1'b0), .s(add_1_s));  // open: c_o
  Multiplexer #(.Selector_Bits(2), .Bits(4)) multiplexer_1 (
    .sel(Store_Clear_Load_Increment), .in_0(4'b0000), .in_1(Input), .in_2(Output), .in_3(add_1_s),
    .out(multiplexer_1_out));
  D_FF d_ff_1 (.D(multiplexer_1_out[3]), .C(clock), .Q(Output[3]));  // open: nQ
  D_FF d_ff_2 (.D(multiplexer_1_out[2]), .C(clock), .Q(Output[2]));  // open: nQ
  D_FF d_ff_3 (.D(multiplexer_1_out[1]), .C(clock), .Q(Output[1]));  // open: nQ
  D_FF d_ff_4 (.D(multiplexer_1_out[0]), .C(clock), .Q(Output[0]));  // open: nQ

  // Notes on the sheet:
  //   Store_Clear_Load_Increment: 0 -> clear
  //   1 -> store input
  //   2 -> load
  //   3 -> increment
endmodule
